# Fritzing sketch FlashyDelayTrigger (saved by Fritzing 1.0.3b)
breadboards: 1

parts:
  M1 = Arduino Nano (Rev3.0)
  Optocoupler_HCPL-817 = Sharp PC817 [package=THT]
  R5 = Resistor [tolerance=±5% resistance=220 package="2010 [SMD]"]
  R7 = Resistor [tolerance=±10% resistance=1k package="2010 [SMD]"]
  NPN_1A = TRANSISTOR_NPN_2 [package=to-92]
  LED_used_as_Photodiode = LED - 5mm [color="White (6500K)" current=0.030A package="5 mm [THT]"]
  X-Sync_OUT = mystery part, 2 pins [chip_label=?]
  X-Sync_IN = Pushbutton [package=THT]
  Rotary_Encoder = Rotary Encoder [package=THT]
  R6 = Resistor [tolerance=±5% resistance=220 package="2010 [SMD]"]
  Press_Rotary = Pushbutton [package=THT]
  WeMos_D1_Mini_OLED_Shield1 = WeMos D1 Mini OLED Shield  # not connected

nets:
  N1: M1.GND, Optocoupler_HCPL-817.Pin_2, R7.Pin_1, X-Sync_IN.leg0, Rotary_Encoder.EncoderPinC, Press_Rotary.leg1
  N2: M1.D2, X-Sync_IN.leg1
  N3: M1.D4, R5.Pin_0
  N4: M1.D6, Press_Rotary.leg0
  N5: M1.D7, Rotary_Encoder.EncoderPinB
  N6: M1.D8, Rotary_Encoder.EncoderPinA
  N7: M1.A0, R7.Pin_0, LED_used_as_Photodiode.anode
  N8: M1.3V3, LED_used_as_Photodiode.cathode
  N9: Optocoupler_HCPL-817.Pin_1, R5.Pin_1
  N10: Optocoupler_HCPL-817.Pin_4, NPN_1A.C, X-Sync_OUT.pin1
  N11: Optocoupler_HCPL-817.Pin_3, R6.Pin_1
  N12: NPN_1A.B, R6.Pin_0
  N13: NPN_1A.E, X-Sync_OUT.pin2
